# Fritzing sketch knocklock (saved by Fritzing 0.9.0b)

parts:
  Часть1 = Troyka Shield
  Часть2 = Troyka Button
  Часть3 = Troyka Buzzer
  Часть4 = Troyka Led
  Часть5 = Troyka Potentiometer
  J1 = Basic Servo
  Часть6 = Arduino Uno (Rev3)  # not connected
  Часть7 = Troyka Sound Loudness Sensor

nets:
  N1: Часть1.D3, Часть2.S
  N2: Часть1.D5, J1.pulse
  N3: Часть1.D8, Часть4.S
  N4: Часть1.D9, Часть3.S
  N5: Часть1.VCC3, Часть2.V
  N6: Часть1.VCC5, J1.vcc
  N7: Часть1.VCC8, Часть4.V
  N8: Часть1.VCC9, Часть3.V
  N9: Часть1.GND3, Часть2.G
  GND5: Часть1.GND5, J1.gnd
  N10: Часть1.GND8, Часть4.G
  N11: Часть1.GND9, Часть3.G
  N12: Часть1.SIG_A0, Часть7.S
  N13: Часть1.SIG_A1, Часть5.S
  N14: Часть1.VCC0, Часть7.V
  N15: Часть1.VCC1, Часть5.V
  N16: Часть1.GND0, Часть7.G
  N17: Часть1.GND1, Часть5.G
